// Logisim project counter.circ as structural Verilog: 3 circuits, main circuit main
module main (
  input  C,
  output A0,
  output A1,
  output A2,
  output A3,
  output A4
);

  wire and_1_out, and_2_out, and_3_out, and_4_out, and_5_out, jktriggerwithreset_1_not_q,
       jktriggerwithreset_2_not_q, jktriggerwithreset_3_not_q, jktriggerwithreset_4_not_q,
       jktriggerwithreset_5_not_q, not_1_out, not_2_out, not_3_out;

  jkTriggerWithReset jktriggerwithreset_1 (
    .j(1'b1), .c(C), .k(1'b1), .reset(and_3_out), .Q(A0), .not_Q(jktriggerwithreset_1_not_q));
  and and_1 (and_1_out, 1'b1, A0);
  jkTriggerWithReset jktriggerwithreset_2 (
    .j(and_1_out), .c(C), .k(and_1_out), .reset(and_3_out), .Q(A1), .not_Q(jktriggerwithreset_2_not_q));
  and and_2 (and_2_out, A0, 1'b1, A1);
  not not_1 (not_1_out, jktriggerwithreset_5_not_q);
  not not_2 (not_2_out, jktriggerwithreset_3_not_q);
  not not_3 (not_3_out, jktriggerwithreset_2_not_q);
  and and_3 (and_3_out, not_1_out, jktriggerwithreset_4_not_q, not_2_out, not_3_out, jktriggerwithreset_1_not_q, C);
  jkTriggerWithReset jktriggerwithreset_3 (
    .j(and_2_out), .c(C), .k(and_2_out), .reset(and_3_out), .Q(A2), .not_Q(jktriggerwithreset_3_not_q));
  and and_4 (and_4_out, A1, A0, 1'b1, A2);
  jkTriggerWithReset jktriggerwithreset_4 (
    .j(and_4_out), .c(C), .k(and_4_out), .reset(and_3_out), .Q(A3), .not_Q(jktriggerwithreset_4_not_q));
  and and_5 (and_5_out, A2, A1, A0, 1'b1, A3);
  jkTriggerWithReset jktriggerwithreset_5 (
    .j(and_5_out), .c(C), .k(and_5_out), .reset(and_3_out), .Q(A4), .not_Q(jktriggerwithreset_5_not_q));

  // Notes on the sheet:
  //   j
  //   c
  //   k
  //   r
  //   First bit
  //   Q
  //   not Q
  //   j
  //   c
  //   k
  //   r
  //   Second bit
  //   Q
  //   not Q
  //   j
  //   c
  //   k
  //   r
  //   A5
  //   A3
  //   A2
  //   A1
  //   Third bit
  //   A4
  //   c
  //   Resetting element
  //   Q
  //   not Q
  //   j
  //   c
  //   k
  //   r
  //   Fourth bit
  //   Q
  //   not Q
  //   j
  //   c
  //   k
  //   r
  //   Fifth bit
  //   Output
  //   bits
  //   Q
  //   not Q
endmodule

// RS Sync
module rsTriggerSync (
  input  S,
  input  c,
  input  R,
  output Q,
  output not_Q
);

  wire and_1_out, and_2_out, nor_2_out, por_1_out;

  and and_1 (and_1_out, S, c);
  and and_2 (and_2_out, c, R);
  nor nor_1 (Q, and_2_out, not_Q);
  nor nor_2 (nor_2_out, Q, and_1_out);
  POR por_1 (.out(por_1_out));
  or or_1 (not_Q, nor_2_out, por_1_out);
endmodule

// JK
module jkTriggerWithReset (
  input  j,
  input  c,
  input  k,
  input  reset,
  output Q,
  output not_Q
);

  wire and_1_out, and_2_out, and_3_out, and_4_out, not_1_out, not_2_out, not_3_out, or_1_out, or_2_out,
       rstriggersync_1_not_q, rstriggersync_1_q;

  and and_1 (and_1_out, not_Q, j);
  not not_1 (not_1_out, reset);
  and and_2 (and_2_out, k, Q);
  and and_3 (and_3_out, and_1_out, not_1_out);
  or or_1 (or_1_out, reset, and_2_out);
  not not_2 (not_2_out, reset);
  rsTriggerSync rstriggersync_1 (
    .S(and_3_out), .c(c), .R(or_1_out), .Q(rstriggersync_1_q), .not_Q(rstriggersync_1_not_q));
  not not_3 (not_3_out, c);
  and and_4 (and_4_out, not_2_out, rstriggersync_1_q);
  or or_2 (or_2_out, rstriggersync_1_not_q, reset);
  rsTriggerSync rstriggersync_2 (.S(or_2_out), .c(not_3_out), .R(and_4_out), .Q(not_Q), .not_Q(Q));

  // Notes on the sheet:
  //   S
  //   c
  //   R
  //   Q
  //   S
  //   c
  //   R
endmodule
