// Logisim project lfsr.circ as structural Verilog: 4 circuits, main circuit main
module main (
  input  A8,
  input  A7,
  input  A6,
  input  A5,
  input  A4,
  input  A3,
  input  A2,
  input  A1,
  input  A0,
  input  cInit,
  input  C,
  output A8_2,
  output A7_2,
  output A6_2,
  output A5_2,
  output A4_2,
  output A3_2,
  output A2_2,
  output A1_2,
  output A0_2
);

  wire and_1_out, and_2_out, and_3_out, and_4_out, and_5_out, and_6_out, and_7_out, and_8_out, and_9_out,
       dtriggersync_1_q, dtriggersync_2_q, dtriggersync_3_q, dtriggersync_4_q, dtriggersync_5_q,
       dtriggersync_6_q, dtriggersync_7_q, dtriggersync_8_q, dtriggersync_9_q, xorfor4inputs_1_out_5;

  and and_1 (and_1_out, A8, cInit);
  and and_2 (and_2_out, A7, cInit);
  and and_3 (and_3_out, A6, cInit);
  and and_4 (and_4_out, A5, cInit);
  and and_5 (and_5_out, A4, cInit);
  and and_6 (and_6_out, A3, cInit);
  and and_7 (and_7_out, A2, cInit);
  and and_8 (and_8_out, A1, cInit);
  and and_9 (and_9_out, A0, cInit);
  or or_1 (A0_2, and_9_out, dtriggersync_1_q);
  dTriggerSync dtriggersync_1 (.D(xorfor4inputs_1_out_5), .c(C), .Q(dtriggersync_1_q));  // open: not_Q
  dTriggerSync dtriggersync_2 (.D(A0_2), .c(C), .Q(dtriggersync_2_q));  // open: not_Q
  or or_2 (A1_2, and_8_out, dtriggersync_2_q);
  dTriggerSync dtriggersync_3 (.D(A1_2), .c(C), .Q(dtriggersync_3_q));  // open: not_Q
  or or_3 (A2_2, and_7_out, dtriggersync_3_q);
  or or_4 (A3_2, and_6_out, dtriggersync_4_q);
  dTriggerSync dtriggersync_4 (.D(A2_2), .c(C), .Q(dtriggersync_4_q));  // open: not_Q
  dTriggerSync dtriggersync_5 (.D(A3_2), .c(C), .Q(dtriggersync_5_q));  // open: not_Q
  or or_5 (A4_2, and_5_out, dtriggersync_5_q);
  dTriggerSync dtriggersync_6 (.D(A4_2), .c(C), .Q(dtriggersync_6_q));  // open: not_Q
  or or_6 (A5_2, and_4_out, dtriggersync_6_q);
  or or_7 (A6_2, and_3_out, dtriggersync_7_q);
  dTriggerSync dtriggersync_7 (.D(A5_2), .c(C), .Q(dtriggersync_7_q));  // open: not_Q
  dTriggerSync dtriggersync_8 (.D(A6_2), .c(C), .Q(dtriggersync_8_q));  // open: not_Q
  or or_8 (A7_2, and_2_out, dtriggersync_8_q);
  or or_9 (A8_2, and_1_out, dtriggersync_9_q);
  dTriggerSync dtriggersync_9 (.D(A7_2), .c(C), .Q(dtriggersync_9_q));  // open: not_Q
  XORfor4inputs xorfor4inputs_1 (.in_2(A4_2), .in_3(A3_2), .in_4(A2_2), .in_1(A8_2), .out_5(xorfor4inputs_1_out_5));

  // Notes on the sheet:
  //   Инициализация
endmodule

module rsTriggerSync (
  input  S,
  input  c,
  input  R,
  output Q,
  output not_Q
);

  wire and_1_out, and_2_out, nor_2_out, por_1_out;

  and and_1 (and_1_out, S, c);
  and and_2 (and_2_out, c, R);
  nor nor_1 (Q, and_2_out, not_Q);
  nor nor_2 (nor_2_out, Q, and_1_out);
  POR por_1 (.out(por_1_out));
  or or_1 (not_Q, nor_2_out, por_1_out);
endmodule

module dTriggerSync (
  input  D,
  input  c,
  output Q,
  output not_Q
);

  wire and_1_out, and_2_out, not_1_out, not_2_out, rstriggersync_1_not_q, rstriggersync_1_q;

  and and_1 (and_1_out, not_Q, D);
  not not_1 (not_1_out, D);
  and and_2 (and_2_out, not_1_out, Q);
  rsTriggerSync rstriggersync_1 (
    .S(and_1_out), .c(c), .R(and_2_out), .Q(rstriggersync_1_q), .not_Q(rstriggersync_1_not_q));
  not not_2 (not_2_out, c);
  rsTriggerSync rstriggersync_2 (.S(rstriggersync_1_not_q), .c(not_2_out), .R(rstriggersync_1_q), .Q(not_Q), .not_Q(Q));

  // Notes on the sheet:
  //   S
  //   c
  //   R
  //   S
  //   c
  //   R
endmodule

module XORfor4inputs (
  input  in_1,
  input  in_2,
  input  in_3,
  input  in_4,
  output out_5
);

  wire xor_1_out, xor_2_out;

  xor xor_1 (xor_1_out, in_1, in_2);
  xor xor_2 (xor_2_out, in_3, in_4);
  xor xor_3 (out_5, xor_1_out, xor_2_out);
endmodule
